# Fritzing sketch BB-UNIT (saved by Fritzing 0.9.3b)
circuit board: 11cm x 7cm
breadboards: 1

parts:
  Pololu_A1 = Pololu A4988 [package=SO16]
  Pololu_A2 = Pololu A4988 [package=SO16]
  Pololu_A3 = Pololu A4988 [package=SO16]
  Composant1 = Arduino Mega ADK (Rev3)
  J1 = female pin header, 4 pins [form="♀ (female)"]
  J2 = female pin header, 4 pins [form="♀ (female)"]
  J3 = female pin header, 4 pins [form="♀ (female)"]
  J4 = Screw terminal - 2 pins [package=THT]
  C1 = Electrolytic Capacitor [capacitance=1µF package="100 mil [THT, electrolytic]"]
  C2 = Electrolytic Capacitor [capacitance=1µF package="100 mil [THT, electrolytic]"]
  C3 = Electrolytic Capacitor [capacitance=1µF package="100 mil [THT, electrolytic]"]
  J5 = screw terminal, 6 pins
  J6 = female pin header, 6 pins [form="♀ (female)"]
  J7 = female pin header, 6 pins [form="♀ (female)"]
  J8 = female pin header, 6 pins [form="♀ (female)"]
  Composant2 = NRF24L01+ Breakout Board
  R1 = Resistor [tolerance=±5% resistance=4.7k package=THT]
  J9 = double row female pin header, 6 pins [form="♀ (female)"]
  J10 = double row female pin header, 6 pins [form="♀ (female)"]
  J11 = double row female pin header, 6 pins [form="♀ (female)"]
  R2 = Resistor [tolerance=±5% resistance=4.7k package=THT]
  R3 = Resistor [tolerance=±5% resistance=4.7k package=THT]
  J12 = screw terminal, 8 pins
  J13 = Screw terminal - 2 pins [package=THT]
  J14 = Screw terminal - 2 pins [package=THT]
  R4 = Resistor [tolerance=±5% resistance=220 package=THT]
  R5 = Resistor [tolerance=±5% resistance=220 package=THT]
  LED1 = LED - 3mm [color="Red (633nm)" package="3 mm [THT]"]
  LED2 = LED - 3mm [color="Red (633nm)" package="3 mm [THT]"]
  R6 = Resistor [tolerance=±5% resistance=220 package=THT]
  LED3 = LED - 3mm [color="Red (633nm)" package="3 mm [THT]"]
  J18 = female pin header, 4 pins [form="♀ (female)"]
  J17 = female pin header, 7 pins [form="♀ (female)"]
  J15 = female pin header, 7 pins [form="♀ (female)"]
  J16 = female pin header, 7 pins [form="♀ (female)"]
  J19 = female pin header, 6 pins [form="♀ (female)"]
  R7 = Resistor [tolerance=±5% resistance=4.7k package=THT]
  R8 = Resistor [tolerance=±5% resistance=47k package=THT]
  S1 = Pushbutton [package="[THT]"]
  S2 = Pushbutton [package="[THT]"]
  R9 = Resistor [tolerance=±5% resistance=220 package=THT]

nets:
  N1: Pololu_A1.ENABLE, Composant1.D4_PWM
  N2: Pololu_A1.MS1, J11.pin1
  N3: Pololu_A1.MS2, J11.pin2
  N4: Pololu_A1.MS3, J11.pin3
  N5: Pololu_A1.RESET, Pololu_A1.SLEEP
  N6: Pololu_A1.STEP, Composant1.D3_PWM
  N7: Pololu_A1.DIR, Composant1.D2_PWM
  GND: Pololu_A1.GND, Composant1.GND, C3.-, J7.pin1, J7.pin2, J7.pin3, J7.pin4, J7.pin5, J7.pin6, Composant2.GND, J14.pin2, LED1.anode, LED2.anode, LED3.anode, J18.pin1, J16.pin1, J16.pin2, J16.pin3, J16.pin4, J16.pin5, J16.pin6, J16.pin7, R7.Pin_0, R9.Pin_0
  VDD: Pololu_A1.VDD, Pololu_A2.VDD, Pololu_A3.VDD, Composant1.5V, J8.pin1, J8.pin2, J8.pin3, J8.pin4, J8.pin5, J8.pin6, Composant2.VCC, R1.Pin_1, R2.Pin_1, R3.Pin_1, J14.pin1, J18.pin2, J17.pin1, J17.pin2, J17.pin3, J17.pin4, J17.pin5, J17.pin6, J17.pin7, S2.Pin_3, S2.Pin_4
  N8: Pololu_A1.1B, J1.pin4
  N9: Pololu_A1.1A, J1.pin3
  N10: Pololu_A1.2A, J1.pin2
  N11: Pololu_A1.2B, J1.pin1
  N12: Pololu_A1.VMOT, Pololu_A2.VMOT, Pololu_A3.VMOT, Composant1.VIN, J4.pin2, C1.+, C2.+, C3.+, R8.Pin_1
  N13: Pololu_A2.ENABLE, Composant1.D5_PWM
  N14: Pololu_A2.MS1, J9.pin1
  N15: Pololu_A2.MS2, J9.pin2
  N16: Pololu_A2.MS3, J9.pin3
  N17: Pololu_A2.RESET, Pololu_A2.SLEEP
  N18: Pololu_A2.STEP, Composant1.D6_PWM
  N19: Pololu_A2.DIR, Composant1.D7_PWM
  N20: Pololu_A2.GND, C2.-
  N21: Pololu_A2.1B, J2.pin4
  N22: Pololu_A2.1A, J2.pin3
  N23: Pololu_A2.2A, J2.pin2
  N24: Pololu_A2.2B, J2.pin1
  N25: Pololu_A3.ENABLE, Composant1.D8_PWM
  N26: Pololu_A3.MS1, J10.pin1
  N27: Pololu_A3.MS2, J10.pin2
  N28: Pololu_A3.MS3, J10.pin3
  N29: Pololu_A3.RESET, Pololu_A3.SLEEP
  N30: Pololu_A3.STEP, Composant1.D9_PWM
  N31: Pololu_A3.DIR, Composant1.D10_PWM
  N32: Pololu_A3.GND, J4.pin1, C1.-
  N33: Pololu_A3.1B, J3.pin4
  N34: Pololu_A3.1A, J3.pin3
  N35: Pololu_A3.2A, J3.pin2
  N36: Pololu_A3.2B, J3.pin1
  N37: Composant1.A8, S2.Pin_1, S2.Pin_2, R9.Pin_1
  N38: Composant1.A0, J15.pin1
  N39: Composant1.A1, J15.pin2
  N40: Composant1.A2, J15.pin3
  N41: Composant1.A3, J15.pin4
  N42: Composant1.A4, J15.pin5
  N43: Composant1.A5, J15.pin6
  N44: Composant1.A6, J15.pin7
  N45: Composant1.A7, R7.Pin_1, R8.Pin_0
  N46: Composant1.D21/SCL, J13.pin1
  N47: Composant1.D20/SDA, J13.pin2
  N48: Composant1.D19/RX1, J12.pin1
  N49: Composant1.D18/TX1, J12.pin2
  N50: Composant1.D17/RX2, J12.pin3
  N51: Composant1.D16/TX2, J12.pin4
  N52: Composant1.D15/RX3, J12.pin5
  N53: Composant1.D14/TX3, J12.pin6
  N54: Composant1.D13_PWM, R6.Pin_1
  N55: Composant1.D12_PWM, R5.Pin_1
  N56: Composant1.D11_PWM, R4.Pin_1
  N57: Composant1.RESET, S1.Pin_3, S1.Pin_4
  N58: Composant1.D0/RX0, J12.pin7
  N59: Composant1.D1/TX0, J12.pin8
  N60: Composant1.D22, J6.pin6
  N61: Composant1.D23, J5.pin6
  N62: Composant1.D24, J6.pin5
  N63: Composant1.D25, J5.pin5
  N64: Composant1.D26, J6.pin4
  N65: Composant1.D27, J5.pin4
  N66: Composant1.D28, J6.pin3
  N67: Composant1.D29, J5.pin3
  N68: Composant1.D30, J6.pin2
  N69: Composant1.D31, J5.pin2
  N70: Composant1.D32, J6.pin1
  N71: Composant1.D33, J5.pin1
  N72: Composant1.D36, J18.pin4
  N73: Composant1.D37, J19.pin6
  N74: Composant1.D38, J18.pin3
  N75: Composant1.D39, J19.pin5
  N76: Composant1.D41, J19.pin4
  N77: Composant1.D43, J19.pin3
  N78: Composant1.D45, J19.pin2
  N79: Composant1.D46, Composant2.CE
  N80: Composant1.D47, J19.pin1
  N81: Composant1.D50/MISO, Composant2.MISO
  N82: Composant1.D51/MOSI, Composant2.MOSI
  N83: Composant1.D52/SCK, Composant2.SCK
  N84: Composant1.D53/SS, Composant2.CS
  N85: R1.Pin_0, J9.pin4, J9.pin5, J9.pin6
  N86: J10.pin4, J10.pin5, J10.pin6, R2.Pin_0
  N87: J11.pin4, J11.pin5, J11.pin6, R3.Pin_0
  N88: R4.Pin_0, LED3.cathode
  N89: R5.Pin_0, LED1.cathode
  N90: LED2.cathode, R6.Pin_0

notes:
  GITHUB
  +
  -
  BB-UNIT
  MOUS
