# Fritzing sketch BB-UNIT2 (saved by Fritzing 0.9.3b)
circuit board: 11cm x 7cm
breadboards: 1

parts:
  Pololu_A1 = Pololu A4988 [package=SO16]
  Pololu_A2 = Pololu A4988 [package=SO16]
  J1 = female pin header, 4 pins [form="♀ (female)"]
  J2 = female pin header, 4 pins [form="♀ (female)"]
  Pololu_A3 = Pololu A4988 [package=SO16]
  J3 = female pin header, 4 pins [form="♀ (female)"]
  C1 = Electrolytic Capacitor [capacitance=1µF package="100 mil [THT, electrolytic]"]  # not connected
  C2 = Electrolytic Capacitor [capacitance=1µF package="100 mil [THT, electrolytic]"]
  C3 = Electrolytic Capacitor [capacitance=1µF package="100 mil [THT, electrolytic]"]
  J7 = screw terminal, 6 pins
  J9 = female pin header, 4 pins [form="♀ (female)"]
  J12 = double row female pin header, 12 pins [form="♀ (female)"]
  J13 = double row female pin header, 6 pins [form="♀ (female)"]
  J14 = double row female pin header, 6 pins [form="♀ (female)"]
  J15 = double row female pin header, 6 pins [form="♀ (female)"]
  S1 = Pushbutton [package="[THT]"]
  R3 = Resistor [tolerance=±5% resistance=10k package=THT]
  S2 = Pushbutton [package="[THT]"]
  J20 = female pin header, 4 pins [form="♀ (female)"]
  J21 = Screw terminal - 2 pins [package=THT]
  Composant1 = Arduino Mega 2560 (Rev3)
  S3 = Pushbutton [package="[THT]"]
  R7 = Resistor [tolerance=±5% resistance=10k package=THT]
  R8 = Resistor [tolerance=±5% resistance=220 package=THT]
  R9 = Resistor [tolerance=±5% resistance=220 package=THT]
  R10 = Resistor [tolerance=±5% resistance=220 package=THT]
  R11 = Resistor [tolerance=±5% resistance=220 package=THT]
  R12 = Resistor [tolerance=±5% resistance=220 package=THT]
  LED1 = LED - 3mm [color="Red (633nm)" package="3 mm [THT]"]
  LED3 = LED - 3mm [color="Red (633nm)" package="3 mm [THT]"]
  LED4 = LED - 3mm [color="Red (633nm)" package="3 mm [THT]"]
  LED5 = LED - 3mm [color="Red (633nm)" package="3 mm [THT]"]
  J24 = female pin header, 6 pins [form="♀ (female)"]
  J25 = female pin header, 2 pins [form="♀ (female)"]
  J26 = double row female pin header, 4 pins [form="♀ (female)"]
  LED6 = LED - 3mm [color="Green (570nm)" package="3 mm [THT]"]
  J27 = Screw terminal - 2 pins [package=THT]
  J6 = screw terminal, 3 pins
  J5 = screw terminal, 3 pins
  J28 = female pin header, 4 pins [form="♀ (female)"]
  J29 = female pin header, 4 pins [form="♀ (female)"]
  J30 = female pin header, 4 pins [form="♀ (female)"]
  J31 = female pin header, 4 pins [form="♀ (female)"]
  R14 = Resistor [tolerance=±5% resistance=220 package=THT]
  LED7 = LED - 3mm [color="Red (633nm)" package="3 mm [THT]"]
  LED8 = LED - 3mm [color="Red (633nm)" package="3 mm [THT]"]
  R15 = Resistor [tolerance=±5% resistance=220 package=THT]
  J32 = female pin header, 4 pins [form="♀ (female)"]
  J33 = female pin header, 4 pins [form="♀ (female)"]
  LED2 = LED - 3mm [color="Red (633nm)" package="3 mm [THT]"]
  R16 = Resistor [tolerance=±5% resistance=220 package=THT]
  J34 = female pin header, 4 pins [form="♀ (female)"]

nets:
  N1: Pololu_A1.MS1, J15.pin1
  N2: Pololu_A1.MS2, J15.pin2
  N3: Pololu_A1.MS3, J15.pin3
  N4: Pololu_A1.RESET, Pololu_A1.SLEEP
  N5: Pololu_A1.STEP, Composant1.D26
  N6: Pololu_A1.DIR, Composant1.D24
  GND: Pololu_A1.GND, Pololu_A2.GND, Pololu_A3.GND, C2.-, C3.-, J12.pin7, J12.pin8, J12.pin9, J12.pin10, J12.pin11, J12.pin12, R3.Pin_1, J21.pin2, R7.Pin_1, LED1.cathode, LED3.cathode, LED4.cathode, LED5.cathode, LED6.cathode, J27.pin2, J28.pin2, J29.pin3, J30.pin3, J31.pin3, LED7.cathode, LED8.cathode, J32.pin3, LED2.cathode
  VDD: Pololu_A1.VDD, Pololu_A2.VDD, Pololu_A3.VDD, J9.pin1, J12.pin1, J12.pin2, J12.pin3, J12.pin4, J12.pin5, J12.pin6, J13.pin4, J13.pin5, J13.pin6, J15.pin4, J15.pin5, J15.pin6, S1.Pin_1, S1.Pin_2, J20.pin1, Composant1.5V, S3.Pin_3, J26.pin2, J28.pin1, J29.pin4, J30.pin4, J31.pin4, J32.pin4
  N7: Pololu_A1.1B, J2.pin4
  N8: Pololu_A1.1A, J2.pin3
  N9: Pololu_A1.2A, J2.pin2
  N10: Pololu_A1.2B, J2.pin1
  N11: Pololu_A1.VMOT, Pololu_A2.VMOT, Pololu_A3.VMOT, C2.+, C3.+, J21.pin1, J27.pin1, R16.Pin_1
  N12: Pololu_A2.MS1, J14.pin1
  N13: Pololu_A2.MS2, J14.pin2
  N14: Pololu_A2.MS3, J14.pin3
  N15: Pololu_A2.RESET, Pololu_A2.SLEEP
  N16: Pololu_A2.STEP, Composant1.D4_PWM
  N17: Pololu_A2.DIR, Composant1.D3_PWM
  N18: Pololu_A2.1B, J1.pin4
  N19: Pololu_A2.1A, J1.pin3
  N20: Pololu_A2.2A, J1.pin2
  N21: Pololu_A2.2B, J1.pin1
  N22: Pololu_A3.MS1, J13.pin1
  N23: Pololu_A3.MS2, J13.pin2
  N24: Pololu_A3.MS3, J13.pin3
  N25: Pololu_A3.RESET, Pololu_A3.SLEEP
  N26: Pololu_A3.STEP, Composant1.D8_PWM
  N27: Pololu_A3.DIR, Composant1.D9_PWM
  N28: Pololu_A3.1B, J3.pin4
  N29: Pololu_A3.1A, J3.pin3
  N30: Pololu_A3.2A, J3.pin2
  N31: Pololu_A3.2B, J3.pin1
  N32: J7.pin1, Composant1.D14/TX3
  N33: J7.pin2, Composant1.D15/RX3
  N34: J7.pin3, Composant1.D16_PWM/TX2
  N35: J7.pin4, Composant1.D17_PWM/RX2
  N36: J7.pin5, Composant1.D18/TX1
  N37: J7.pin6, Composant1.D19/RX1
  N38: J9.pin2, S2.Pin_1, S2.Pin_2, J20.pin2, Composant1.GND, J26.pin1, J34.pin3
  N39: J9.pin3, Composant1.D13_PWM
  N40: J9.pin4, Composant1.D12_PWM
  N41: J14.pin4, J14.pin5, J14.pin6
  N42: S1.Pin_3, S1.Pin_4, R3.Pin_0, Composant1.D34
  N43: S2.Pin_3, S2.Pin_4, Composant1.RESET
  N44: J20.pin3, Composant1.D11_PWM
  N45: J20.pin4, Composant1.D10_PWM
  N46: Composant1.A12, J33.pin1
  N47: Composant1.A13, J33.pin2
  N48: Composant1.A14, J33.pin3
  N49: Composant1.A15, J33.pin4
  N50: Composant1.A6, J28.pin3
  N51: Composant1.A7, J28.pin4
  N52: Composant1.D21/SCL, Composant1.SCL, J25.pin1, J29.pin2, J30.pin2, J31.pin2, J32.pin2
  N53: Composant1.D20/SDA, Composant1.SDA, J25.pin2, J29.pin1, J30.pin1, J31.pin1, J32.pin1
  N54: Composant1.D0_RX0, J24.pin6
  N55: Composant1.D1_TX0, J24.pin5
  N56: Composant1.D2_PWM, J24.pin4
  N57: Composant1.D5_PWM, J24.pin3
  N58: Composant1.D6_PWM, J24.pin2
  N59: Composant1.D7_PWM, J24.pin1
  N60: Composant1.D23, J5.pin3
  N61: Composant1.D25, J5.pin2
  N62: Composant1.D27, J5.pin1
  N63: Composant1.D29, J6.pin3
  N64: Composant1.D31, J6.pin2
  N65: Composant1.D33, J6.pin1
  N66: Composant1.D36, S3.Pin_1, S3.Pin_2, R7.Pin_0
  N67: Composant1.D40, R8.Pin_0
  N68: Composant1.D42, R9.Pin_0
  N69: Composant1.D43, J26.pin3
  N70: Composant1.D44, R10.Pin_0
  N71: Composant1.D45, J26.pin4
  N72: Composant1.D46, R11.Pin_0
  N73: Composant1.D48, R12.Pin_0
  N74: Composant1.D50, R14.Pin_0
  N75: Composant1.D51, J34.pin2
  N76: Composant1.D52, R15.Pin_0
  N77: Composant1.D53, J34.pin1
  N78: R8.Pin_1, LED5.anode
  N79: R9.Pin_1, LED4.anode
  N80: R10.Pin_1, LED3.anode
  N81: R11.Pin_1, LED2.anode
  N82: R12.Pin_1, LED1.anode
  N83: LED6.anode, R16.Pin_0
  N84: R14.Pin_1, LED7.anode
  N85: LED8.anode, R15.Pin_1

notes:
  +
  -
  A
  B
  X
  Y
  Z
  -5v+
  github.com/Gruniek/BB-UNIT
  By MOUS
  -BB-
  UNIT
