# Fritzing sketch Slave-Board (saved by Fritzing 0.9.3b)
circuit board: 10cm x 7cm
breadboards: 1

parts:
  Composant1 = Arduino Nano (Rev3.0)
  Pololu_A2 = Pololu A4988 [package=SO16]
  Pololu_A3 = Pololu A4988 [package=SO16]
  J1 = screw terminal, 4 pins
  J2 = screw terminal, 4 pins
  J3 = screw terminal, 4 pins
  J4 = Screw terminal - 2 pins [package=THT]
  C1 = Electrolytic Capacitor [capacitance=1µF package="100 mil [THT, electrolytic]"]
  C2 = Electrolytic Capacitor [capacitance=1µF package="100 mil [THT, electrolytic]"]
  C3 = Electrolytic Capacitor [capacitance=1µF package="100 mil [THT, electrolytic]"]
  Pololu_A1 = Pololu A4988 [package=SO16]
  J5 = Screw terminal - 2 pins [package=THT]
  J6 = double row female pin header, 6 pins [form="♀ (female)"]
  J7 = double row female pin header, 6 pins [form="♀ (female)"]
  J8 = double row female pin header, 6 pins [form="♀ (female)"]
  R1 = Resistor [tolerance=±5% resistance=4.7k package=THT]
  J9 = Screw terminal - 2 pins [package=THT]
  J10 = Screw terminal - 2 pins [package=THT]
  J12 = female pin header, 3 pins [form="♀ (female)"]
  J16 = female pin header, 3 pins [form="♀ (female)"]
  J17 = female pin header, 3 pins [form="♀ (female)"]
  J18 = Screw terminal - 2 pins [package=THT]
  J15 = female pin header, 3 pins [form="♀ (female)"]
  J13 = female pin header, 3 pins [form="♀ (female)"]
  J14 = female pin header, 3 pins [form="♀ (female)"]

nets:
  N1: Composant1.D1/TX, J4.pin2
  N2: Composant1.D0/RX, J4.pin1
  GND: Composant1.GND, Pololu_A2.GND, Pololu_A3.GND, C1.-, C2.-, C3.-, Pololu_A1.GND, J5.pin1, J9.pin2, J16.pin1, J16.pin2, J16.pin3, J14.pin1, J14.pin2, J14.pin3
  N3: Composant1.D2, Pololu_A2.DIR
  N4: Composant1.D3, Pololu_A2.STEP
  N5: Composant1.D4, Pololu_A2.ENABLE, Pololu_A3.ENABLE, Pololu_A1.ENABLE
  N6: Composant1.D5, Pololu_A1.DIR
  N7: Composant1.D6, Pololu_A1.STEP
  N8: Composant1.D7, Pololu_A3.DIR
  N9: Composant1.D8, Pololu_A3.STEP
  N10: Composant1.D9, J13.pin1
  N11: Composant1.D10, J13.pin2
  N12: Composant1.D11/MOSI, J13.pin3
  N13: Composant1.D12/MISO, J18.pin1
  N14: Composant1.VIN, Pololu_A2.VMOT, Pololu_A3.VMOT, C1.+, C2.+, C3.+, Pololu_A1.VMOT, J5.pin2
  VDD: Composant1.5V, Pololu_A2.VDD, Pololu_A3.VDD, Pololu_A1.VDD, R1.Pin_0, J9.pin1, J17.pin1, J17.pin2, J17.pin3, J15.pin1, J15.pin2, J15.pin3
  N15: Composant1.A5, J10.pin1
  N16: Composant1.A4, J10.pin2
  N17: Composant1.A2, J12.pin1
  N18: Composant1.A1, J12.pin2
  N19: Composant1.A0, J12.pin3
  N20: Composant1.D13/SCK, J18.pin2
  N21: Pololu_A2.MS1, J6.pin1
  N22: Pololu_A2.MS2, J6.pin2
  N23: Pololu_A2.MS3, J6.pin3
  N24: Pololu_A2.RESET, Pololu_A2.SLEEP
  N25: Pololu_A2.1B, J3.pin4
  N26: Pololu_A2.1A, J3.pin3
  N27: Pololu_A2.2A, J3.pin2
  N28: Pololu_A2.2B, J3.pin1
  N29: Pololu_A3.MS1, J8.pin1
  N30: Pololu_A3.MS2, J8.pin2
  N31: Pololu_A3.MS3, J8.pin3
  N32: Pololu_A3.RESET, Pololu_A3.SLEEP
  N33: Pololu_A3.1B, J1.pin4
  N34: Pololu_A3.1A, J1.pin3
  N35: Pololu_A3.2A, J1.pin2
  N36: Pololu_A3.2B, J1.pin1
  N37: J2.pin1, Pololu_A1.2B
  N38: J2.pin2, Pololu_A1.2A
  N39: J2.pin3, Pololu_A1.1A
  N40: J2.pin4, Pololu_A1.1B
  N41: Pololu_A1.MS1, J7.pin1
  N42: Pololu_A1.MS2, J7.pin2
  N43: Pololu_A1.MS3, J7.pin3
  N44: Pololu_A1.RESET, Pololu_A1.SLEEP
  N45: J6.pin4, J6.pin5, J6.pin6, J7.pin4, J7.pin5, J7.pin6, J8.pin4, J8.pin5, J8.pin6, R1.Pin_1

notes:
  X
  Y
  Z
  GITHUB -> OPEN-BB-8
  MOUS
  +
  A C
  - +
  -
  NANO
  Rx
